// Logisim project gated_d_latch.circ as structural Verilog: 1 circuit, main circuit main
module main (
  input  Data,
  input  Control,
  output out_3,
  output out_4
);

  wire nand_1_out, nand_2_out, nand_4_out, not_1_out;

  not not_1 (not_1_out, Data);
  nand nand_1 (nand_1_out, Data, Control);
  nand nand_2 (nand_2_out, not_1_out, Control);
  nand nand_3 (out_3, nand_1_out, nand_4_out);
  nand nand_4 (nand_4_out, out_3, nand_2_out);
  LED led_1 (.in(out_3));
  LED led_2 (.in(nand_4_out));
endmodule
