// Logisim project my_logics.circ as structural Verilog: 2 circuits, main circuit ALU
module ALU (
  input  OP1,
  input  [7:0] Bus,
  input  CLK,
  input  NOT,
  input  AND,
  input  OR,
  input  ADD,
  input  SHL,
  output OF,
  output [7:0] RES
);

  wire [2:0] bit_extender_1_out;
  wire [7:0] adder_1_out, and_1_out, controlled_buffer_1_out, not_1_out, or_1_out, register_1_q,
       shifter_1_out;

  Bit_Extender #(.out_width(3)) bit_extender_1 (.in(register_1_q), .out(bit_extender_1_out));
  Register register_1 (.D(Bus), .en(OP1), .Q(register_1_q), .clk(CLK));  // open: clr
  assign not_1_out = ~Bus;  // NOT_Gate not_1, 8 bits wide
  assign and_1_out = Bus & register_1_q;  // AND_Gate and_1, 8 bits wide
  assign or_1_out = Bus | register_1_q;  // OR_Gate or_1, 8 bits wide
  Adder adder_1 (.a(Bus), .b(register_1_q), .out(adder_1_out), .cout(OF));  // open: cin
  Shifter shifter_1 (.in(Bus), .\dist (bit_extender_1_out), .out(shifter_1_out));
  assign controlled_buffer_1_out = NOT ? not_1_out : 8'bz;  // Controlled_Buffer controlled_buffer_1
  assign controlled_buffer_1_out = AND ? and_1_out : 8'bz;  // Controlled_Buffer controlled_buffer_2
  assign controlled_buffer_1_out = OR ? or_1_out : 8'bz;  // Controlled_Buffer controlled_buffer_3
  assign controlled_buffer_1_out = ADD ? adder_1_out : 8'bz;  // Controlled_Buffer controlled_buffer_4
  assign controlled_buffer_1_out = SHL ? shifter_1_out : 8'bz;  // Controlled_Buffer controlled_buffer_5
  Register register_2 (.D(controlled_buffer_1_out), .en(1'b1), .Q(RES), .clk(CLK));  // open: clr
endmodule

module sequencer (
  input  CLK,
  output out_2,
  output out_3,
  output out_4,
  output out_5,
  output out_6,
  output out_7,
  output out_8,
  output out_9
);

  wire d_ff_1_q, d_ff_2_q, d_ff_3_q, d_ff_4_q, d_ff_5_q, d_ff_6_q, d_ff_7_q, d_ff_8_q, d_ff_9_q, d_ff_10_q,
       d_ff_11_q, d_ff_12_q, d_ff_13_q, d_ff_14_q, d_ff_15_q, d_ff_16_q, not_1_out, not_2_out, not_3_out,
       not_4_out, not_5_out, not_6_out, not_7_out, not_8_out, not_9_out, not_10_out, or_1_out, or_2_out;

  not not_1 (not_1_out, CLK);
  or or_1 (or_1_out, not_1_out, d_ff_16_q);
  or or_2 (or_2_out, CLK, d_ff_16_q);
  not not_2 (not_2_out, d_ff_16_q);
  or or_3 (out_2, d_ff_16_q, not_3_out);
  D_Flip_Flop #(.trigger("high")) d_ff_1 (.clk(or_2_out), .D(not_2_out), .Q(d_ff_1_q));  // open: Qn, preset, en, reset
  not not_3 (not_3_out, d_ff_2_q);
  D_Flip_Flop #(.trigger("high")) d_ff_2 (.clk(or_1_out), .D(d_ff_1_q), .Q(d_ff_2_q));  // open: Qn, preset, en, reset
  and and_1 (out_3, d_ff_2_q, not_4_out);
  D_Flip_Flop #(.trigger("high")) d_ff_3 (.clk(or_2_out), .D(d_ff_2_q), .Q(d_ff_3_q));  // open: Qn, preset, en, reset
  not not_4 (not_4_out, d_ff_4_q);
  D_Flip_Flop #(.trigger("high")) d_ff_4 (.clk(or_1_out), .D(d_ff_3_q), .Q(d_ff_4_q));  // open: Qn, preset, en, reset
  not not_5 (not_5_out, d_ff_6_q);
  and and_2 (out_4, d_ff_4_q, not_5_out);
  D_Flip_Flop #(.trigger("high")) d_ff_5 (.clk(or_2_out), .D(d_ff_4_q), .Q(d_ff_5_q));  // open: Qn, preset, en, reset
  D_Flip_Flop #(.trigger("high")) d_ff_6 (.clk(or_1_out), .D(d_ff_5_q), .Q(d_ff_6_q));  // open: Qn, preset, en, reset
  and and_3 (out_5, d_ff_6_q, not_6_out);
  D_Flip_Flop #(.trigger("high")) d_ff_7 (.clk(or_2_out), .D(d_ff_6_q), .Q(d_ff_7_q));  // open: Qn, preset, en, reset
  not not_6 (not_6_out, d_ff_8_q);
  D_Flip_Flop #(.trigger("high")) d_ff_8 (.clk(or_1_out), .D(d_ff_7_q), .Q(d_ff_8_q));  // open: Qn, preset, en, reset
  not not_7 (not_7_out, d_ff_10_q);
  and and_4 (out_6, d_ff_8_q, not_7_out);
  D_Flip_Flop #(.trigger("high")) d_ff_9 (.clk(or_2_out), .D(d_ff_8_q), .Q(d_ff_9_q));  // open: Qn, preset, en, reset
  D_Flip_Flop #(.trigger("high")) d_ff_10 (.clk(or_1_out), .D(d_ff_9_q), .Q(d_ff_10_q));  // open: Qn, preset, en, reset
  and and_5 (out_7, d_ff_10_q, not_8_out);
  D_Flip_Flop #(.trigger("high")) d_ff_11 (
    .clk(or_2_out), .D(d_ff_10_q), .Q(d_ff_11_q));  // open: Qn, preset, en, reset
  not not_8 (not_8_out, d_ff_12_q);
  D_Flip_Flop #(.trigger("high")) d_ff_12 (
    .clk(or_1_out), .D(d_ff_11_q), .Q(d_ff_12_q));  // open: Qn, preset, en, reset
  not not_9 (not_9_out, d_ff_14_q);
  and and_6 (out_8, d_ff_12_q, not_9_out);
  D_Flip_Flop #(.trigger("high")) d_ff_13 (
    .clk(or_2_out), .D(d_ff_12_q), .Q(d_ff_13_q));  // open: Qn, preset, en, reset
  D_Flip_Flop #(.trigger("high")) d_ff_14 (
    .clk(or_1_out), .D(d_ff_13_q), .Q(d_ff_14_q));  // open: Qn, preset, en, reset
  and and_7 (out_9, d_ff_14_q, not_10_out);
  D_Flip_Flop #(.trigger("high")) d_ff_15 (
    .clk(or_2_out), .D(d_ff_14_q), .Q(d_ff_15_q));  // open: Qn, preset, en, reset
  not not_10 (not_10_out, d_ff_16_q);
  D_Flip_Flop #(.trigger("high")) d_ff_16 (
    .clk(or_1_out), .D(d_ff_15_q), .Q(d_ff_16_q));  // open: Qn, preset, en, reset
endmodule
