// Logisim project playground.circ as structural Verilog: 1 circuit, main circuit main
module main (
  input  [7:0] in_1,
  input  in_2,
  input  in_3,
  input  in_4,
  input  in_5,
  input  in_6,
  input  in_7,
  output [7:0] out_8
);

  wire alu_1_of, clock_1_out;

  LED led_1 (.in(alu_1_of));
  ALU alu_1 (
    .OP1(in_3), .Bus(in_1), .CLK(clock_1_out), .NOT(in_2), .AND(in_4), .OR(in_5), .ADD(in_6), .SHL(in_7),
    .OF(alu_1_of), .RES(out_8));
  Clock clock_1 (.out(clock_1_out));
endmodule
